// Digital circuit alu.dig as structural Verilog
module alu (
  input  [3:0] func,
  input  [31:0] a,
  input  [31:0] b,
  output [31:0] c
);

  wire [0:0] comparator_1_lt, comparator_2_lt;
  wire [31:0] add_1_s, and_1_out, barrelshifter_1_out, barrelshifter_2_out, barrelshifter_3_out,
       multiplexer_1_out, multiplexer_2_out, or_1_out, sub_1_s, xor_1_out;

  Add #(.Bits(32)) add_1 (.a(a), .b(b), .c_i(1'b0), .s(add_1_s));  // open: c_o
  Sub #(.Bits(32)) sub_1 (.a(a), .b(b), .c_i(1'b0), .s(sub_1_s));  // open: c_o
  Comparator #(.Signed("true"), .Bits(32)) comparator_1 (.a(a), .b(b), .lt(comparator_1_lt[0]));  // open: gt, eq
  Comparator #(.Bits(32)) comparator_2 (.a(a), .b(b), .lt(comparator_2_lt[0]));  // open: gt, eq
  assign or_1_out = a | b;  // Or or_1, 32 bits wide
  assign and_1_out = a & b;  // And and_1, 32 bits wide
  Multiplexer #(.Bits(32)) multiplexer_1 (.sel(func[3]), .in_0(add_1_s), .in_1(sub_1_s), .out(multiplexer_1_out));
  BarrelShifter #(.Bits(32)) barrelshifter_1 (.in(a), .shift(b[5:0]), .out(barrelshifter_1_out));
  assign xor_1_out = a ^ b;  // XOr xor_1, 32 bits wide
  BarrelShifter #(.Bits(32), .direction("right")) barrelshifter_2 (.in(a), .shift(b[5:0]), .out(barrelshifter_2_out));
  BarrelShifter #(.Bits(32), .barrelShifterMode("arithmetic"), .direction("right")) barrelshifter_3 (
    .in(a), .shift(b[5:0]), .out(barrelshifter_3_out));
  Multiplexer #(.Bits(32)) multiplexer_2 (
    .sel(func[3]), .in_0(barrelshifter_2_out), .in_1(barrelshifter_3_out), .out(multiplexer_2_out));
  Multiplexer #(.Selector_Bits(3), .Bits(32)) multiplexer_3 (
    .sel(func[2:0]), .in_0(multiplexer_1_out), .in_1(barrelshifter_1_out),
    .in_2({{31{1'b0}}, comparator_1_lt[0]}), .in_3({{31{1'b0}}, comparator_2_lt[0]}), .in_4(xor_1_out),
    .in_5(multiplexer_2_out), .in_6(or_1_out), .in_7(and_1_out), .out(c));

  // Notes on the sheet:
  //   sll
  //   slt
  //   sltu
  //   srl
  //   sra
endmodule
