// Digital circuit branch.dig as structural Verilog
module branch (
  input  [31:0] r1,
  input  [31:0] r2,
  input  [2:0] func3,
  output branch
);

  wire comparator_1_eq, comparator_1_lt, comparator_2_lt, not_1_out, not_2_out, not_3_out;

  Comparator #(.Signed("true"), .Bits(32)) comparator_1 (
    .a(r1), .b(r2), .eq(comparator_1_eq), .lt(comparator_1_lt));  // open: gt
  Comparator #(.Bits(32)) comparator_2 (.a(r1), .b(r2), .lt(comparator_2_lt));  // open: gt, eq
  not not_1 (not_1_out, comparator_1_eq);
  not not_2 (not_2_out, comparator_1_lt);
  not not_3 (not_3_out, comparator_2_lt);
  Multiplexer #(.Selector_Bits(3)) multiplexer_1 (
    .sel(func3), .in_0(comparator_1_eq), .in_1(not_1_out), .in_2(1'b0), .in_3(1'b0), .in_4(comparator_1_lt),
    .in_5(not_2_out), .in_6(comparator_2_lt), .in_7(not_3_out), .out(branch));
endmodule
