// Digital circuit code.dig as structural Verilog
module code (
  input  [31:0] addr,
  output [31:0] inst
);

  wire comparator_1_eq;

  Comparator #(.Bits(20)) comparator_1 (.a(addr[31:12]), .b({20{1'b0}}), .eq(comparator_1_eq));  // open: gt, lt
  ROM #(.AddrBits(10), .Bits(32)) rom_1 (.A(addr[11:2]), .sel(comparator_1_eq), .D(inst));

  // Notes on the sheet:
  //   contents of rom_1 (hex, n*v repeats v):
  //   20000113,5c0006f,200293,451c663,ffc10113,112023,ffc10113,312023
  //   ,fff18193,fe9ff0ef,12183,410113,ffc10113,412023,ffe18193,fd1ff0ef
  //   ,12183,410113,12083,410113,320233,8067,18233,8067,200193,fa5ff0ef
endmodule
