// Digital circuit controller.dig as structural Verilog
module controller (
  input  [6:0] opcode,
  input  [2:0] func3,
  input  [6:0] func7,
  output [1:0] regSrc,
  output srcB,
  output [3:0] aluFunc,
  output regWrite,
  output memWrite,
  output jmp,
  output branch,
  output srcA,
  output [1:0] immSrc
);

  controller #(.applicationType("IVERILOG")) u_controller (
    .opcode(opcode), .func3(func3), .func7(func7), .regSrc(regSrc), .regWrite(regWrite), .memWrite(memWrite),
    .aluFunc(aluFunc), .jmp(jmp), .branch(branch), .srcA(srcA), .srcB(srcB), .immSrc(immSrc));
  // Pins of 1 and 2 bits meet at regSrc
endmodule

/* Code of controller:
module controller(
	opcode, func3, func7, 
	regSrc, regWrite, memWrite, aluFunc,jmp, branch, srcA, srcB, immSrc);

	input [6:0] opcode;
	input [2:0] func3;
	input [6:0] func7;

	output [1:0] regSrc;
	output regWrite, memWrite;
	output [3:0] aluFunc;
	output jmp, branch, srcA, srcB;
	output [1:0] immSrc;

	wire load, store, jal, jalr, b, r_type,i_type, lui, auipc;

	assign lui = opcode == 7'b01_101_11;
	assign auipc = opcode == 7'b00_101_11;

	assign load  = (opcode == 7'b00_000_11)?1:0;
	assign store = (opcode == 7'b01_000_11)?1:0;
	assign jal = (opcode == 7'b11_011_11)?1:0;
	assign jalr = (opcode == 7'b11_001_11)?1:0;
	assign b = (opcode == 7'b11_000_11)?1:0;
	assign r_type = (opcode == 7'b01_100_11)?1:0;
	assign i_type = (opcode == 7'b00_100_11)?1:0;

	assign aluFunc =  r_type ? {func7[5:5],func3}: i_type?{1'b0,func3}:0;

	assign jmp = jal || jalr;
	assign branch = b;

	assign regWrite = jal || jalr || r_type || i_type || lui || auipc || load;

	assign srcA = auipc|| jal || b;
	assign srcB = ~r_type;

	assign memWrite = store;
	assign regSrc = load ? 1 :
			(jal || jalr)?2:0;

	assign immSrc = b? 1: 
			(lui || auipc) ? 2:
		        jal? 3: 0;

endmodule
*/
