// Digital circuit data-hazard.dig as structural Verilog
module data_hazard (
  input  [4:0] e_rs1,
  input  [4:0] e_rs2,
  input  [4:0] m_rd,
  input  [4:0] w_rd,
  input  m_regWrite,
  input  w_regWrite,
  output [1:0] fwA,
  output [1:0] fwB
);

  forward forward_1 (.rs(e_rs1), .m_rd(m_rd), .w_rd(w_rd), .m_regWrite(m_regWrite), .w_regWrite(w_regWrite), .fw(fwA));
  forward forward_2 (.rs(e_rs2), .m_rd(m_rd), .w_rd(w_rd), .m_regWrite(m_regWrite), .w_regWrite(w_regWrite), .fw(fwB));
endmodule
