// Digital circuit data.dig as structural Verilog
module data (
  input  [31:0] addr,
  input  clk,
  input  we,
  input  [31:0] din,
  input  [2:0] func3,
  output [31:0] dout
);

  wire and_1_out, comparator_1_eq;
  wire [7:0] multiplexer_1_out;
  wire [15:0] multiplexer_2_out;
  wire [31:0] bitextender_1_out, bitextender_2_out, multiplexer_3_out, multiplexer_4_out, ramdualport_1_d;

  Comparator #(.Bits(16)) comparator_1 (.a(addr[31:16]), .b({16{1'b0}}), .eq(comparator_1_eq));  // open: gt, lt
  and and_1 (and_1_out, we, comparator_1_eq);
  RAMDualPort #(.AddrBits(14), .Bits(32)) ramdualport_1 (
    .A(addr[15:2]), .Din(din), .str(and_1_out), .C(clk), .ld(comparator_1_eq), .D(ramdualport_1_d));
  Multiplexer #(.Selector_Bits(2), .Bits(8)) multiplexer_1 (
    .sel(addr[1:0]), .in_0(ramdualport_1_d[7:0]), .in_1(ramdualport_1_d[15:8]),
    .in_2(ramdualport_1_d[23:16]), .in_3(ramdualport_1_d[31:24]), .out(multiplexer_1_out));
  Multiplexer #(.Bits(16)) multiplexer_2 (
    .sel(addr[1]), .in_0(ramdualport_1_d[15:0]), .in_1(ramdualport_1_d[31:16]), .out(multiplexer_2_out));
  BitExtender #(.outputBits(32)) bitextender_1 (.in(multiplexer_1_out), .out(bitextender_1_out));
  BitExtender #(.inputBits(16), .outputBits(32)) bitextender_2 (.in(multiplexer_2_out), .out(bitextender_2_out));
  Multiplexer #(.Bits(32)) multiplexer_3 (
    .sel(func3[2]), .in_0(bitextender_1_out), .in_1({{24{1'b0}}, multiplexer_1_out}), .out(multiplexer_3_out));
  Multiplexer #(.Bits(32)) multiplexer_4 (
    .sel(func3[2]), .in_0(bitextender_2_out), .in_1({{16{1'b0}}, multiplexer_2_out}), .out(multiplexer_4_out));
  Multiplexer #(.Selector_Bits(2), .Bits(32)) multiplexer_5 (
    .sel(func3[1:0]), .in_0(multiplexer_3_out), .in_1(multiplexer_4_out), .in_2(ramdualport_1_d),
    .in_3({32{1'b0}}), .out(dout));
endmodule
