// Digital circuit f-d.dig as structural Verilog
module f_d (
  input  clk,
  input  flush,
  input  stall,
  input  [63:0] din,
  output [63:0] dout
);

  r #(.applicationType("IVERILOG")) u_r (.clk(clk), .clr(flush), .stall(stall), .din(din[31:0]), .dout(dout[31:0]));
  // Pins of 32 and 64 bits meet at din
  // Pins of 32 and 64 bits meet at dout
endmodule

/* Code of r:
module r(clk, clr, stall, din, dout);
	input clk, clr, stall;
	input [31:0] din;
	output [31:0] dout;
	
	reg [31:0] dout;

	always @(posedge clk)
	begin
		if(clr)
			dout = 0;
		else  if(~stall)
			dout = din;
	end
endmodule
*/
