// Digital circuit forward.dig as structural Verilog
module forward (
  input  [4:0] rs,
  input  [4:0] m_rd,
  input  [4:0] w_rd,
  input  m_regWrite,
  input  w_regWrite,
  output [1:0] fw
);

  forward #(.applicationType("IVERILOG")) u_forward (
    .rs(rs), .m_rd(m_rd), .w_rd(w_rd), .m_write(m_regWrite), .w_write(w_regWrite), .fw(fw));
endmodule

/* Code of forward:
module forward(rs,m_rd, w_rd,m_write, w_write, fw);
	input [4:0] rs, m_rd, w_rd;
	input m_write, w_write;
	output [1:0] fw;

	reg [1:0] fw;
	wire not0;

	assign not0 = (rs == 0)?0:1;

	always @(rs, m_rd, w_rd, m_write, w_write, not0)
	begin
		if(not0 && m_write && rs == m_rd)
			fw = 2;
		else if(not0 && w_write && rs == w_rd)
			fw = 1;
		else
			fw = 0;

	end

endmodule
*/
