// Digital circuit imm.dig as structural Verilog
module imm (
  input  [31:0] inst,
  output [31:0] load_i_jalr_imm,
  output [31:0] branch_imm,
  output [31:0] store_imm,
  output [31:0] lui_auipc_imm,
  output [31:0] jal_imm,
  output [6:0] opcode,
  output [2:0] func3,
  output [6:0] func7,
  output [4:0] rs1,
  output [4:0] rs2,
  output [4:0] rd
);

  BitExtender #(.inputBits(21), .outputBits(32)) bitextender_1 (
    .in({inst[31], inst[19:12], inst[20], inst[30:21], 1'b0}), .out(jal_imm));
  BitExtender #(.inputBits(12), .outputBits(32)) bitextender_2 (.in(inst[31:20]), .out(load_i_jalr_imm));
  BitExtender #(.inputBits(12), .outputBits(32)) bitextender_3 (.in({inst[31:25], inst[11:7]}), .out(store_imm));
  BitExtender #(.inputBits(13), .outputBits(32)) bitextender_4 (
    .in({inst[31], inst[7], inst[30:25], inst[11:8], 1'b0}), .out(branch_imm));

  assign func3 = inst[14:12];
  assign func7 = inst[31:25];
  assign lui_auipc_imm = {inst[31:12], {12{1'b0}}};
  assign opcode = inst[6:0];
  assign rd = inst[11:7];
  assign rs1 = inst[19:15];
  assign rs2 = inst[24:20];

  // Notes on the sheet:
  //   sw imm
  //   beq imm
  //   opcode
  //   funct3
  //   funct7
  //   rs1
  //   rs2
  //   rd
endmodule
