// Digital circuit load-harzard.dig as structural Verilog
module load_harzard (
  input  [4:0] d_rs1,
  input  [4:0] d_rs2,
  input  [4:0] e_rd,
  input  [1:0] e_regSrc,
  input  e_pcSrc,
  output stallF,
  output stallD,
  output flushD,
  output flushE
);

  wire comparator_1_eq, comparator_2_eq, comparator_3_eq, or_1_out;

  Comparator #(.Bits(5)) comparator_1 (.a(d_rs1), .b(e_rd), .eq(comparator_1_eq));  // open: gt, lt
  Comparator #(.Bits(5)) comparator_2 (.a(d_rs2), .b(e_rd), .eq(comparator_2_eq));  // open: gt, lt
  Comparator #(.Bits(2)) comparator_3 (.a(e_regSrc), .b(2'b01), .eq(comparator_3_eq));  // open: gt, lt
  or or_1 (or_1_out, comparator_1_eq, comparator_2_eq);
  and and_1 (stallD, or_1_out, comparator_3_eq);
  or or_2 (flushE, stallD, e_pcSrc);

  assign flushD = e_pcSrc;
  assign stallF = stallD;
endmodule
