// Digital circuit main.dig as structural Verilog
module main (
  input  clk,
  input  rst,
  input  clk_2
);

  wire and_1_out, branch_cond_branch, code_1_p2, controller_1_p10, controller_1_p11, data_1_p6, decode_p2,
       decode_p4, inst_p2, inst_p3, inst_p5, load_harzard_1_flushe, load_harzard_1_stallf, not_1_out,
       or_1_out, r2_p5;
  wire [1:0] controller_1_p4, controller_1_p12, data_hazard_1_fwa, data_hazard_1_fwb, f_d_1_p5_3;
  wire [3:0] controller_1_p7;
  wire [4:0] decode_p5, decode_p6, f_d_1_p5_2, f_d_2_p5_2, f_d_3_p5;
  wire [7:0] counter_1_out;
  wire [27:10] decode_p7;
  wire [31:0] a_p5, alu_1_c, aluResult_2_p5, aluResult_p5, b_p5, decode_p8, decode_p9, decode_p10,
       decode_p11, decode_p12, f_d_1_p5, f_d_2_p5, mem_din, memData_p5, multiplexer_1_out, multiplexer_2_out,
       multiplexer_3_out, multiplexer_4_out, multiplexer_5_out, multiplexer_6_out, multiplexer_7_out, pc,
       pc_2_p5, pc_4_1_pc4, pc_plus_4_4_p5, reg_din, regfile_1_r1, regfile_1_r2;
  wire [31:5] f_d_3_p5_2;
  wire [63:0] pc_plus_4_2_dout, pc_plus_4_3_dout, pc_plus_4_p5;

  Multiplexer #(.Bits(32)) multiplexer_1 (.sel(or_1_out), .in_0(pc_4_1_pc4), .in_1(alu_1_c), .out(multiplexer_1_out));
  pc pc_1 (.clk(clk_2), .rst(rst), .stall(load_harzard_1_stallf), .din(multiplexer_1_out), .dout(pc));
  Counter #(.Bits(8)) counter_1 (.en(1'b1), .C(clk_2), .clr(1'b0), .out(counter_1_out));  // open: ovf
  // code code_1: pin names not known; wires that end beside it: pc, code_1_p2
  pc_4 pc_4_1 (.pc(pc), .pc4(pc_4_1_pc4));
  Seven_Seg_Hex seven_seg_hex_1 (.d(counter_1_out[7:4]), .dp(1'b0));
  Seven_Seg_Hex seven_seg_hex_2 (.d(counter_1_out[3:0]), .dp(1'b0));
  // f_d inst: pin names not known; wires that end beside it: clk_2, inst_p2, inst_p3, code_1_p2, inst_p5
  // f_d pc_2: pin names not known; wires that end beside it: clk_2, inst_p2, inst_p3, pc, pc_2_p5
  // f_d pc_plus_4: pin names not known; wires that end beside it: clk_2, inst_p2, inst_p3, pc_4_1_pc4, pc_plus_4_p5
  // imm decode: pin names not known; wires that end beside it: inst_p5, decode_p2, decode_p7[27:25], decode_p4, decode_p5, decode_p6, decode_p7[14:10], decode_p8, decode_p9, decode_p10, decode_p11, decode_p12
  Seven_Seg_Hex seven_seg_hex_3 (.d(pc[7:4]), .dp(1'b0));
  Seven_Seg_Hex seven_seg_hex_4 (.d(pc[3:0]), .dp(1'b0));
  not not_1 (not_1_out, clk_2);
  Seven_Seg_Hex seven_seg_hex_5 (.d(reg_din[23:20]), .dp(1'b0));
  // controller controller_1: pin names not known; wires that end beside it: decode_p2, decode_p7[27:25], decode_p4, controller_1_p4, decode_p7[17], decode_p7[18], controller_1_p7, decode_p7[23], decode_p7[24], controller_1_p10, controller_1_p11, controller_1_p12
  regfile regfile_1 (
    .clk(not_1_out), .we(f_d_3_p5_2[7]), .rs1(decode_p5), .rs2(decode_p6), .rd(f_d_3_p5), .din(reg_din),
    .r1(regfile_1_r1), .r2(regfile_1_r2));
  Multiplexer #(.Bits(32)) multiplexer_2 (
    .sel(decode_p7[18]), .in_0(decode_p10), .in_1(decode_p11), .out(multiplexer_2_out));
  Seven_Seg_Hex seven_seg_hex_6 (.d(reg_din[19:16]), .dp(1'b0));
  Multiplexer #(.Selector_Bits(2), .Bits(32)) multiplexer_3 (
    .sel(controller_1_p12), .in_0(multiplexer_2_out), .in_1(decode_p12), .in_2(decode_p8), .in_3(decode_p9),
    .out(multiplexer_3_out));
  Seven_Seg_Hex seven_seg_hex_7 (.d(reg_din[15:12]), .dp(1'b0));
  Multiplexer #(.Bits(32)) multiplexer_4 (
    .sel(controller_1_p10), .in_0(regfile_1_r1), .in_1(pc_2_p5), .out(multiplexer_4_out));
  Multiplexer #(.Bits(32)) multiplexer_5 (
    .sel(controller_1_p11), .in_0(regfile_1_r2), .in_1(multiplexer_3_out), .out(multiplexer_5_out));
  Seven_Seg_Hex seven_seg_hex_8 (.d(reg_din[11:8]), .dp(1'b0));
  load_harzard load_harzard_1 (
    .d_rs1(decode_p5), .d_rs2(decode_p6), .e_rd(f_d_1_p5_2), .e_regSrc(f_d_1_p5_3), .e_pcSrc(or_1_out),
    .stallF(load_harzard_1_stallf), .stallD(inst_p3), .flushD(inst_p2), .flushE(load_harzard_1_flushe));
  Seven_Seg_Hex seven_seg_hex_9 (.d(reg_din[7:4]), .dp(1'b0));
  // f_d f_d_1: pin names not known; wires that end beside it: clk_2, load_harzard_1_flushe, 1'b0, {4'b0000, decode_p7[27:23], controller_1_p7, decode_p7[18:17], controller_1_p4, decode_p7[14:10], decode_p6, decode_p5}, {f_d_1_p5[31:17], f_d_1_p5_3, f_d_1_p5_2, f_d_1_p5[9:0]}
  // f_d a: pin names not known; wires that end beside it: clk_2, load_harzard_1_flushe, 1'b0, multiplexer_4_out, a_p5
  // f_d b: pin names not known; wires that end beside it: clk_2, load_harzard_1_flushe, 1'b0, multiplexer_5_out, b_p5
  // f_d r2: pin names not known; wires that end beside it: clk_2, load_harzard_1_flushe, 1'b0, regfile_1_r2, r2_p5
  f_d pc_plus_4_2 (
    .clk(clk_2), .flush(load_harzard_1_flushe), .stall(1'b0), .din(pc_plus_4_p5), .dout(pc_plus_4_2_dout));
  Seven_Seg_Hex seven_seg_hex_10 (.d(reg_din[3:0]), .dp(1'b0));
  Multiplexer #(.Selector_Bits(2), .Bits(32)) multiplexer_6 (
    .sel(data_hazard_1_fwa), .in_0(a_p5), .in_1(reg_din), .in_2(aluResult_p5), .in_3(a_p5),
    .out(multiplexer_6_out));
  Multiplexer #(.Selector_Bits(2), .Bits(32)) multiplexer_7 (
    .sel(data_hazard_1_fwb), .in_0(b_p5), .in_1(reg_din), .in_2(aluResult_p5), .in_3(b_p5),
    .out(multiplexer_7_out));
  Seven_Seg_Hex seven_seg_hex_11 (.d(mem_din[15:12]), .dp(1'b0));
  Seven_Seg_Hex seven_seg_hex_12 (.d(mem_din[11:8]), .dp(1'b0));
  data_hazard data_hazard_1 (
    .e_rs1(f_d_1_p5[4:0]), .e_rs2(f_d_1_p5[9:5]), .m_rd(f_d_2_p5_2), .w_rd(f_d_3_p5),
    .m_regWrite(f_d_2_p5[17]), .w_regWrite(f_d_3_p5_2[7]), .fwA(data_hazard_1_fwa), .fwB(data_hazard_1_fwb));
  branch branch_cond (
    .func3(f_d_1_p5[27:25]), .r1(multiplexer_6_out), .r2(multiplexer_7_out), .branch(branch_cond_branch));
  alu alu_1 (.func(f_d_1_p5[22:19]), .a(multiplexer_6_out), .b(multiplexer_7_out), .c(alu_1_c));
  Seven_Seg_Hex seven_seg_hex_13 (.d(mem_din[7:4]), .dp(1'b0));
  and and_1 (and_1_out, f_d_1_p5[24], branch_cond_branch);
  Seven_Seg_Hex seven_seg_hex_14 (.d(mem_din[3:0]), .dp(1'b0));
  or or_1 (or_1_out, f_d_1_p5[23], and_1_out);
  // f_d f_d_2: pin names not known; wires that end beside it: clk_2, 1'b0, 1'b0, {{10{1'b0}}, f_d_1_p5[27:25], f_d_1_p5[18:17], f_d_1_p5_3, f_d_1_p5_2, f_d_1_p5[9:0]}, {f_d_2_p5[31:15], f_d_2_p5_2, f_d_2_p5[9:0]}
  // f_d aluResult: pin names not known; wires that end beside it: clk_2, 1'b0, 1'b0, alu_1_c, aluResult_p5
  // f_d r2_2: pin names not known; wires that end beside it: clk_2, 1'b0, 1'b0, r2_p5, mem_din
  f_d pc_plus_4_3 (.clk(clk_2), .flush(1'b0), .stall(1'b0), .din(pc_plus_4_2_dout), .dout(pc_plus_4_3_dout));
  // data data_1: pin names not known; wires that end beside it: clk_2, f_d_2_p5[18], aluResult_p5, f_d_2_p5[21:19], mem_din, data_1_p6
  // f_d f_d_3: pin names not known; wires that end beside it: clk_2, 1'b0, 1'b0, {{24{1'b0}}, f_d_2_p5[17:15], f_d_2_p5_2}, {f_d_3_p5_2, f_d_3_p5}
  // f_d memData: pin names not known; wires that end beside it: clk_2, 1'b0, 1'b0, data_1_p6, memData_p5
  // f_d aluResult_2: pin names not known; wires that end beside it: clk_2, 1'b0, 1'b0, aluResult_p5, aluResult_2_p5
  // f_d pc_plus_4_4: pin names not known; wires that end beside it: clk_2, 1'b0, 1'b0, pc_plus_4_3_dout, pc_plus_4_4_p5
  Multiplexer #(.Selector_Bits(2), .Bits(32)) multiplexer_8 (
    .sel(f_d_3_p5_2[6:5]), .in_0(aluResult_2_p5), .in_1(memData_p5), .in_2(pc_plus_4_4_p5),
    .in_3(aluResult_2_p5), .out(reg_din));

  // Notes on the sheet:
  //   clk_2: Hz: 20
  //   clk
  //   pc
  //   reg
  //   mem
endmodule
