// Digital circuit pc.dig as structural Verilog
module pc (
  input  clk,
  input  rst,
  input  [31:0] din,
  input  stall,
  output [31:0] dout
);

  pc #(.applicationType("IVERILOG")) u_pc (.clk(clk), .rst(rst), .stall(stall), .din(din), .dout(dout));
endmodule

/* Code of pc:
module pc(clk, rst, stall, din, dout);
	input clk, rst, stall;
	input [31:0] din;
	output [31:0] dout;

	reg [31:0] dout;

	always @(posedge clk)
	begin
		if(rst)
			dout = 0;
		else if(~stall)
			dout = din;
	end
endmodule
*/
