// Digital circuit single-main.dig as structural Verilog
module single_main (
  input  rst,
  input  clk
);

  wire and_1_out, branch_1_branch, controller_1_p5, controller_1_p6, controller_1_p8, controller_1_p9,
       controller_1_p10, controller_1_p11, or_1_out;
  wire [1:0] controller_1_p4, controller_1_p12;
  wire [2:0] decode_func3;
  wire [3:0] controller_1_p7;
  wire [4:0] decode_rd, decode_rs1, decode_rs2;
  wire [6:0] decode_func7, decode_opcode;
  wire [7:0] counter_1_out;
  wire [31:0] alu_1_c, code_1_inst, data_1_dout, decode_branch_imm, decode_jal_imm, decode_load_i_jalr_imm,
       decode_lui_auipc_imm, decode_store_imm, mem_din, multiplexer_1_out, multiplexer_2_out,
       multiplexer_3_out, multiplexer_4_out, multiplexer_5_out, pc, pc_4_1_pc4, reg_din, regfile_1_r1;

  Counter #(.Bits(8)) counter_1 (.en(1'b1), .C(clk), .clr(1'b0), .out(counter_1_out));  // open: ovf
  Multiplexer #(.Bits(32)) multiplexer_1 (.sel(or_1_out), .in_0(pc_4_1_pc4), .in_1(alu_1_c), .out(multiplexer_1_out));
  pc pc_1 (.clk(clk), .rst(rst), .stall(1'b0), .din(multiplexer_1_out), .dout(pc));
  Seven_Seg_Hex seven_seg_hex_1 (.d(counter_1_out[7:4]), .dp(1'b0));
  Seven_Seg_Hex seven_seg_hex_2 (.d(counter_1_out[3:0]), .dp(1'b0));
  code code_1 (.addr(pc), .inst(code_1_inst));
  pc_4 pc_4_1 (.pc(pc), .pc4(pc_4_1_pc4));
  imm decode (
    .inst(code_1_inst), .opcode(decode_opcode), .func3(decode_func3), .func7(decode_func7), .rs1(decode_rs1),
    .rs2(decode_rs2), .rd(decode_rd), .lui_auipc_imm(decode_lui_auipc_imm), .jal_imm(decode_jal_imm),
    .load_i_jalr_imm(decode_load_i_jalr_imm), .store_imm(decode_store_imm), .branch_imm(decode_branch_imm));
  Seven_Seg_Hex seven_seg_hex_3 (.d(pc[7:4]), .dp(1'b0));
  Seven_Seg_Hex seven_seg_hex_4 (.d(pc[3:0]), .dp(1'b0));
  // controller controller_1: pin names not known; wires that end beside it: decode_opcode, decode_func3, decode_func7, controller_1_p4, controller_1_p5, controller_1_p6, controller_1_p7, controller_1_p8, controller_1_p9, controller_1_p10, controller_1_p11, controller_1_p12
  regfile regfile_1 (
    .clk(clk), .we(controller_1_p5), .rs1(decode_rs1), .rs2(decode_rs2), .rd(decode_rd), .din(reg_din),
    .r1(regfile_1_r1), .r2(mem_din));
  Multiplexer #(.Bits(32)) multiplexer_2 (
    .sel(controller_1_p6), .in_0(decode_load_i_jalr_imm), .in_1(decode_store_imm), .out(multiplexer_2_out));
  Multiplexer #(.Selector_Bits(2), .Bits(32)) multiplexer_3 (
    .sel(controller_1_p12), .in_0(multiplexer_2_out), .in_1(decode_branch_imm), .in_2(decode_lui_auipc_imm),
    .in_3(decode_jal_imm), .out(multiplexer_3_out));
  Seven_Seg_Hex seven_seg_hex_5 (.d(reg_din[23:20]), .dp(1'b0));
  Seven_Seg_Hex seven_seg_hex_6 (.d(reg_din[19:16]), .dp(1'b0));
  Seven_Seg_Hex seven_seg_hex_7 (.d(reg_din[15:12]), .dp(1'b0));
  Multiplexer #(.Bits(32)) multiplexer_4 (
    .sel(controller_1_p10), .in_0(regfile_1_r1), .in_1(pc), .out(multiplexer_4_out));
  Multiplexer #(.Bits(32)) multiplexer_5 (
    .sel(controller_1_p11), .in_0(mem_din), .in_1(multiplexer_3_out), .out(multiplexer_5_out));
  Seven_Seg_Hex seven_seg_hex_8 (.d(reg_din[11:8]), .dp(1'b0));
  // Probe on decode_func3
  // Probe on multiplexer_5_out
  Seven_Seg_Hex seven_seg_hex_9 (.d(reg_din[7:4]), .dp(1'b0));
  branch branch_1 (.func3(decode_func3), .r1(regfile_1_r1), .r2(mem_din), .branch(branch_1_branch));
  alu alu_1 (.func(controller_1_p7), .a(multiplexer_4_out), .b(multiplexer_5_out), .c(alu_1_c));
  Seven_Seg_Hex seven_seg_hex_10 (.d(reg_din[3:0]), .dp(1'b0));
  and and_1 (and_1_out, controller_1_p9, branch_1_branch);
  data data_1 (
    .clk(clk), .we(controller_1_p6), .addr(alu_1_c), .func3(decode_func3), .din(mem_din), .dout(data_1_dout));
  Seven_Seg_Hex seven_seg_hex_11 (.d(mem_din[15:12]), .dp(1'b0));
  or or_1 (or_1_out, controller_1_p8, and_1_out);
  Seven_Seg_Hex seven_seg_hex_12 (.d(mem_din[11:8]), .dp(1'b0));
  Multiplexer #(.Selector_Bits(2), .Bits(32)) multiplexer_6 (
    .sel(controller_1_p4), .in_0(alu_1_c), .in_1(data_1_dout), .in_2(pc_4_1_pc4), .in_3(alu_1_c),
    .out(reg_din));
  Seven_Seg_Hex seven_seg_hex_13 (.d(mem_din[7:4]), .dp(1'b0));
  Seven_Seg_Hex seven_seg_hex_14 (.d(mem_din[3:0]), .dp(1'b0));

  // Notes on the sheet:
  //   clk: Hz: 200
  //   clk
  //   pc
  //   reg
  //   mem
endmodule
